# Fritzing sketch dgtf-hardware-setup (saved by Fritzing 0.8.5b)
breadboards: 1

parts:
  R1 = Rotary Potentiometer (Small) [maximum_resistance=100kΩ package=THT]
  J1 = Piezo Speaker
  S1 = Pushbutton [package=THT]
  Part1 = Photon

nets:
  N1: R1.leg1, J1.pin1, S1.leg0, Part1.GND
  N2: R1.wiper, Part1.A0
  N3: R1.leg2, Part1.3V3
  N4: J1.pin2, Part1.D0
  N5: S1.leg1, Part1.D6
